# Fritzing sketch TemperatureSpeaker (saved by Fritzing 0.9.3b)
breadboards: 1

parts:
  IC1 = PIC16F690 [package="DIP (Dual Inline) [THT]"]
  LED1 = LED - 5mm [color="Red (633nm)" package="5 mm [THT]"]
  J1 = PIC ICSP - 5 pins [form="♂ (male)" package=THT]
  R1 = Resistor [tolerance=±5% resistance=10k package=THT]
  XTAL1 = Crystal [frequency="16 Mhz" package=THT]
  S1 = Pushbutton [package=THT]
  R2 = Resistor [tolerance=±5% resistance=5.2k package=THT]
  R3 = Resistor [tolerance=±5% resistance=10k package=THT]
  R4 = Resistor [tolerance=±5% resistance=220 package=THT]
  U1 = mystery part, 3 pins [chip_label=LM335]
  U2 = mystery part, 3 pins [chip_label=TLE2426]
  R5 = Trimmer Potentiometer [maximum_resistance=100kΩ package=THT]
  D1 = Rectifier Diode [part_number=1N4001 package="300 mil [THT]"]
  D2 = Rectifier Diode [part_number=1N4001 package="300 mil [THT]"]
  R7 = Resistor [tolerance=±5% resistance=1k package=THT]
  U3 = OP37 - Low Noise, Precision, High Speed Op Amp [part_number=OP37]
  R8 = Resistor [tolerance=±5% resistance=1M package=THT]
  R9 = Resistor [tolerance=±5% resistance=1M package=THT]
  R6 = Resistor [tolerance=±5% resistance=27 package=THT]

nets:
  N1: IC1.VDD, J1.pin2, R1.Pin_0, R2.Pin_0, R3.Pin_0, U2.pin1, U2.pin3, D1.anode, D2.anode, U3.+IN, U3.V+
  N2: IC1.RA5, XTAL1.pin_0
  N3: IC1.RA4, XTAL1.pin_1
  N4: IC1.RA3, J1.pin1, R1.Pin_1, S1.leg0
  N5: IC1.RC0, LED1.anode
  N6: IC1.RA2, U3.OUT, R8.Pin_0, R9.Pin_0
  N7: IC1.RA1, J1.pin5
  N8: IC1.RA0, J1.pin4
  N9: IC1.VSS, LED1.cathode, J1.pin3, S1.leg1, R4.Pin_0, U1.pin2, U2.pin2, U3.-V
  N10: R2.Pin_1, U1.pin3
  N11: R3.Pin_1, R5.leg2, D1.cathode
  N12: R4.Pin_1, R5.leg1, D2.cathode
  N13: R5.wiper, R6.Pin_0
  N14: R7.Pin_1, U3.-IN, R8.Pin_1, R9.Pin_1, R6.Pin_1

notes:
  Thermocouple

custom parts:
  PIC16F690: PIC® Flash microcontroller mid-range x14 architecture 2.0-5.5 volts, internal oscillator 8 MHz - 32 KHz, EEPROM, nanoWatt Technology. 12 channels of 10-bit A/D, two comparators, on-chip voltage reference, Enhanced Capture/Compare/PWM, EUSART, SPI/I2C.
  PIC ICSP - 5 pins: PIC ICSP programmer connection (ICP01 PICkit 2 sw)
