# Fritzing sketch TemperatureSpeakerKom (saved by Fritzing 0.9.3b)
circuit board: 13.5398cm x 9.15531cm
breadboards: 2

parts:
  R1 = Resistor [tolerance=±5% resistance=2.2k package=THT]
  C1 = Ceramic Capacitor [capacitance=10nF package="100 mil [THT, multilayer]"]
  R2 = Resistor [tolerance=±5% resistance=4.7k package=THT]
  R3 = Resistor [tolerance=±5% resistance=4.7k package=THT]
  C2 = Ceramic Capacitor [capacitance=10nF package="100 mil [THT, multilayer]"]
  C3 = Ceramic Capacitor [capacitance=100nF package="100 mil [THT, multilayer]"]
  R4 = Resistor [tolerance=±5% resistance=10k package=THT]
  J1 = Piezo Speaker
  IC2 = PIC16F690 [package="DIP (Dual Inline) [THT]"]
  J2 = PIC ICSP - 5 pins [form="♂ (male)" package=THT]
  R10 = Resistor [tolerance=±5% resistance=10k package=THT]
  S2 = Pushbutton [package=THT]
  R11 = Resistor [tolerance=±5% resistance=5.2k package=THT]
  R12 = Resistor [tolerance=±5% resistance=10k package=THT]
  R13 = Resistor [tolerance=±5% resistance=220 package=THT]
  U4 = mystery part, 3 pins [chip_label=LM335]
  U5 = mystery part, 3 pins [chip_label=TLE2426]
  R14 = Trimmer Potentiometer [maximum_resistance=100kΩ package=THT]
  D3 = Rectifier Diode [part_number=1N4001 package="300 mil [THT]"]
  D4 = Rectifier Diode [part_number=1N4001 package="300 mil [THT]"]
  R15 = Resistor [tolerance=±5% resistance=27 package=THT]
  R16 = Resistor [tolerance=±5% resistance=1k package=THT]
  U6 = OP37 - Low Noise, Precision, High Speed Op Amp [part_number=OP37]
  R17 = Resistor [tolerance=±5% resistance=1M package=THT]
  R18 = Resistor [tolerance=±5% resistance=1M package=THT]
  LED2 = LED - 5mm [color="Red (633nm)" package="5 mm [THT]"]
  T1 = LM35 Temperature Sensor [package="TO92 [THT]"]
  U7 = mystery part, 2 pins [chip_label="Xtal 14.7456 MHz"]
  IC3 = 24LC512 [package=THT]

nets:
  N1: R1.Pin_0, IC2.VDD, J2.pin2, R10.Pin_0, R11.Pin_0, R12.Pin_0, U5.pin1, U5.pin3, D3.anode, D4.anode, R16.Pin_0, U6.+IN, U6.V+, T1.+Vs, T1.Vout, IC3.WP_-_Write_Protect, IC3.+V
  N2: R1.Pin_1, IC2.RB4, IC3.SDA_-_I2C_Data
  N3: C1.0, R2.Pin_0, R3.Pin_0
  N4: C1.1, IC2.VSS, J2.pin3, S2.leg1, R13.Pin_0, U4.pin2, U5.pin2, U6.-V, LED2.cathode, IC3.A0, IC3.A1, IC3.A2, IC3.0V
  N5: R2.Pin_1, IC2.RC5
  N6: R3.Pin_1, C2.1, C3.1
  N7: C2.0, R4.Pin_1, J1.pin2
  N8: C3.0, R4.Pin_0, J1.pin1
  N9: IC2.RA5, U7.pin1
  N10: IC2.RA4, U7.pin2
  N11: IC2.RA3, J2.pin1, R10.Pin_1, S2.leg0
  N12: IC2.RB6, IC3.SCL_-_I2C_Clock
  N13: IC2.RC0, LED2.anode
  N14: IC2.RA2, U6.OUT, R17.Pin_0, R18.Pin_0
  N15: IC2.RA1, J2.pin5
  N16: IC2.RA0, J2.pin4
  N17: R11.Pin_1, U4.pin3
  N18: R12.Pin_1, R14.leg2, D4.cathode
  N19: R13.Pin_1, R14.leg1, D3.cathode
  N20: R14.wiper, R15.Pin_0
  N21: R15.Pin_1, R16.Pin_1, U6.-IN, R17.Pin_1, R18.Pin_1

notes:
  Thermocouple
  Pictalker breadboard
  TempertureSensore breadboard
  Sound unit
  EEPROM
  Picprocessor
  Button

custom parts:
  PIC16F690: PIC® Flash microcontroller mid-range x14 architecture 2.0-5.5 volts, internal oscillator 8 MHz - 32 KHz, EEPROM, nanoWatt Technology. 12 channels of 10-bit A/D, two comparators, on-chip voltage reference, Enhanced Capture/Compare/PWM, EUSART, SPI/I2C.
  PIC ICSP - 5 pins: PIC ICSP programmer connection (ICP01 PICkit 2 sw)

// code stored in the sketch: test.ino


// code stored in the sketch: Untitled4.ino
/* Cc5x C-compiler */
#include "16F690.h"
#include "int16Cxx.h"
#pragma config |= 0x00D2  /* use HS-XTAL 14.7456 MHz */
#pragma bit scl_IIC @ PORTB.6 
#pragma bit sda_IIC @ PORTB.4 

#define  WRITE_sda() TRISB.4 = 0 // SDA must be output when writing
#define  READ_sda()  TRISB.4 = 1 // SDA must be input when reading
#pragma codepage 0

/* Function prototypes */
void ADinit( void );
void delay10( char );

void ack_polling(void);
void start(void);
void stop(void);
char read_byte(void);
void send_byte(char);
char read_eeprom(char, char);
void write_eeprom(char, char, char);
char phonemestart_hi(char);
char phonemestart_lo(char);

char sentence(char);
/* The following two functions are written by ourselves */
void picTalkerTest(); 
void ADconverterTest();

#pragma rambank 1
char message[61];  // must be long enough for the message
char mode;
char index;
char phoneme;
unsigned long count;

#pragma origin 4
/* interrupt routine                      */
/* TIMER2 is servoupdating PWM at 7200 Hz */
interrupt int_server( void ) 
{
  int_save_registers
  char sv_FSR = FSR;       // save FSR
  char sv_PCLATH = PCLATH; // save PCLATH
  /* mode=0 => wait, ready to talk        */
  /* mode=1 => get next phoneme or pause  */
  /* mode=2 => initiate for pause         */
  /* mode=3 => initiate for phoneme       */
  /* mode=4 => go on with the pause       */
  /* mode=5 => go on with the phoneme     */
 
  char pwm_byte, address_hi, address_lo;
  pwm_byte = 128; // idle value

  switch(mode)
    {
       case 0: // wait for talk
        {
          index = 0;
          break;
        }

       case 1: // get new phoneme or pause
        phoneme = message[index];
       	message[index] = 0xFF; // to clean up the array
        index++;  // phoneme is read, so update the index

        if(phoneme == 0xFF) // 0xFF means end of message
          {
            index = 0;
            mode = 0;
            break;
          }

        if(phoneme < 5) // means it is a pause
           {            
             mode = 2;
             break;
           }
 
        /* so it must be a phoneme  */
             mode = 3;
             break;          

       case 2: // initiate pause
        if(phoneme == 0) count = 72;   //  10 ms
        if(phoneme == 1) count = 216;  //  30 ms
        if(phoneme == 2) count = 360;  //  50 ms
        if(phoneme == 3) count = 720;  // 100 ms
        if(phoneme == 4) count = 1440; // 200 ms
        mode = 4; // next time, go on with the pause
        break;

       case 3: // initiate phoneme
        /* Random address read */
        address_hi = phonemestart_hi(phoneme-5);
        address_lo = phonemestart_lo(phoneme-5);
        pwm_byte = read_eeprom(address_hi, address_lo);
        mode = 5; // next time, go on with the phoneme
        break;

       case 4: //  go on with pause
        count--;
        if(count==0) mode = 1; // next time new phoneme/pause
        break;

       case 5: // go on with phoneme
        /* Current adress read, automatic increment */
        start();
        send_byte(0xA1);
        pwm_byte = read_byte(); // phoneme data
        stop();
        if(pwm_byte == 0) // means end of phoneme data
         {
           mode = 1; // next time new phoneme/pause
           pwm_byte = 128;
         }
        break;
    }

  /* update PWM  */
  CCP1CON.4 = pwm_byte.0;
  CCP1CON.5 = pwm_byte.1;
  pwm_byte /= 4;
  CCPR1L = pwm_byte; 

  /* return from the interrupt */
  TMR2IF = 0; 
  PCLATH = sv_PCLATH;    // restore PCLATH
  FSR = sv_FSR;          // restore FSR
  int_restore_registers
}

void main(void) {
   /* Setting up ports */
  TRISC.0 = 0; // lightdiode at RC0 is output
  PORTC.0 = 0; // no light
 
  ANSELH  = 0 ; // PORTB digital
  PORTB.4 = 0 ; // PORTB.4 pending "0" 
  TRISB.4 = 1 ; // simulated open collector
  TRISB.6 = 0 ; // SCL output 
  TRISC.5 = 0 ; // CCP PWM output
  TRISA.3 = 1 ; // SW1 input

  ADinit();
  delay10(100); 
  /* Setup TIMER2 */
  /*
    0.xxxx.x.xx  - unimplemented
    x.1000.x.xx  Postscaler 8
    x.xxxx.1.xx  TMR2 is on
    x.xxxx.x.00  Prescaler 1
  */
  T2CON = 0b0.1000.1.00;
  
  /* Setup CCP1 PWM-mode  */ 
  /*
    00.xx.xxxx  Single PWM output
    xx.00.xxxx  PWM Duty Two LSB
    xx.xx.1100  11xx when Single PWM-mode
  */
  CCP1CON = 0b00.00.1100 ; 

  PR2 = 0x3F; // gives the highest PWM frequency for 8 bit resolution
  mode = 0;   // no talking yet
  TMR2IE  = 1;   /* local enable  */
  PEIE    = 1;   /* peripherals enable */
  GIE     = 1;   /* global enable */
  index =0;
  ADconverterTest();
  delay10(100);
  picTalkerTest(); // adds "We speak not only to be heard but to be understood" to message[]
	
	/* The following while-loop is written by ourselves */
  while(1){
  	if (mode != 0) PORTC.0 = 1; // LED on when talking
  	else PORTC.0 = 0;
  	while (PORTA.3); // wait for button press
	ADconverterTest();
	delay10(100);
	picTalkerTest();
	while (!PORTA.3); // wait for button release
  }
}

void ADconverterTest(){
	unsigned long advalue;
	GO=1;
    while(GO);
    advalue = ADRESH*256;
    advalue += ADRESL;

    if (advalue){
    	char i;
    	for (i = 0; i < 6; i++){
    		if (i % 2)
    			PORTC.0 = 0;
    		else
    			PORTC.0 = 1;
    		delay10(100);
    	}
    }
}

void picTalkerTest() {
	char i, ch;
    for(i=0;;i++)
     {
       ch=sentence(i);
       message[i]=ch;
       if(ch==0xFF)break;  
     }
     mode = 1; // start talking

}

/* "We speak not only to be heard but to be understood" */
char sentence( char index)
{
  skip(index);
  return 0x37; // zero 
  return 0x13;
  return 0x0E;
  return 0x17;
  return 0x04;
  
  return 0x2E; // one
  return 0x20;
  return 0x1B;
  return 0x04;
  
  return 0x0D; // two 
  return 0x16;
  return 0x16;
  return 0x04;
  
  return 0x1D; // three 
  return 0x0E;
  return 0x13;
  return 0x04;
  
  return 0x28; // four 
  return 0x3A;
  return 0x04;
  
  return 0x28; // five 
  return 0x06;
  return 0x23;
  return 0x04;
  
  return 0x37; // six 
  return 0x13;
  return 0x29;
  return 0x37;
  return 0x04;
  
  return 0x37; // seven 
  return 0x13;
  return 0x23;
  return 0x13;
  return 0x1D;
  return 0x04;
  
  return 0x14; // eight
  return 0x0D;
  return 0x04;
  
  return 0x38; // nine
  return 0x06;
  return 0x1D;
  return 0xFF;
	
}


/* *********************************** */
/*     FUNCTIONS FOR ADCONVERTER       */
/* *********************************** */


/* **** ADconverter function ************** */
void ADinit( void )
{
  // AD setup 
  ANSEL.2 = 1; // RA2 AN2 analog configurated
  TRISA.2=1;   // AN2 input

  ADCON1 = 0b0.101.0000; // AD conversion clock 'fosc/16'

  /* 
     1.x.xxxx.x.x  ADRESH:ADRESL is 10 bit right justified
     x.0.xxxx.x.x  Vref is Vdd
     x.x.0010.x.x  Channel (AN2) 
     x.x.xxxx.0.x  Go/!Done - start from program later
     x.x.xxxx.x.1  Enable AD-converter
  */
  ADCON0 = 0b1.0.0010.0.1; 
}

/* **** delay function **** */

void delay10( char n)
{
    char i;
    OPTION = 7;
    do  {  i = TMR0 + 39; /* 256 microsec * 39 = 10 ms */
        while ( i != TMR0) ;
    } while ( --n > 0);
}

/* ************************************************* */
/*              FUNCTIONS FOR PICTALKER              */
/* ************************************************* */

/* opcodes are for the chip SP256                */
/* the code "0xFF" is used as "end of sentence"  */
#pragma codepage 2

/*
    I2C interface for 24LC512    
    Nathan Seidle
    nathan.seidle@colorado.edu
    
    minor changes by William Sandqvist
    to work with the pictalk.c program
    william@kth.se   
*/

/* The extra nop()'s are needed if compiled with optimization */

//=================
//Make sure the bits agree with the TRISB statements

//=================
void ack_polling(void)
{
    //wait for chip to respond
    //cycles 17 times to complete
    //write cycle at 4MHz
    while(sda_IIC != 0)
    {
        start();
        send_byte(0xA0);
    }
    stop();
}

void write_eeprom(char address_hi, char address_lo, char data)
{
    start();
    send_byte(0xA0);
    send_byte(address_hi);
    send_byte(address_lo);
    send_byte(data);
    stop();
}

char read_eeprom(char address_hi, char address_lo)
{
   
    char byte;

    start();
    send_byte(0xA0); // control byte = write
    send_byte(address_hi);
    send_byte(address_lo);
    stop();

    start();
    send_byte(0xA1); // control byte = read
    byte = read_byte();
    stop();
    
    return byte;
}

void start(void)
{
    WRITE_sda();
    sda_IIC = 0;
}

void stop(void)
{
    scl_IIC = 0;

    WRITE_sda();
    sda_IIC = 0;
    // nop();
    // nop(); 
    nop();
    nop();
    scl_IIC = 1;
    // nop();
    // nop(); 
    nop();
    sda_IIC = 1;
}

char read_byte(void)
{
    char j, in_byte;

    scl_IIC = 0;

    READ_sda();

    for(j = 0 ; j < 8 ; j++)
    {
        scl_IIC = 0;
        // nop();
        // nop();
        // nop();
        nop();
        scl_IIC = 1;

        in_byte = rl(in_byte);
        in_byte.0 = sda_IIC;
    }

    return in_byte;
}

void send_byte(char out_byte)
{
    char i;

    WRITE_sda();

    for( i = 0 ; i < 8 ; i++ )
    {
        out_byte = rl(out_byte);
        scl_IIC = 0;
        sda_IIC = Carry;
        scl_IIC = 1;
        nop();
    }

    //read ack.
    scl_IIC = 0;
    READ_sda();
    scl_IIC = 1;
}

/* lookup tables for allphone start adresses in the I2C-EEPROM        */
/* all allphone data ends with "0" in the I2C-EEPROM                  */
/* pauses 0x00, 0x01, 0x02, 0x03, 0x04 are not stored in EEPROM       */
/* so opcodes for SP256 with the offset of -5 should be used as index */

char phonemestart_hi(char index)
{
  skip(index);
  return 0x00; // 0x05  OY  as in vOIce
  return 0x09; // 0x06  AY  as in kIte
  return 0x0E; // 0x07  EH  as in End
  return 0x10; // 0x08  KK3 as in Crane
  return 0x13; // 0x09  PP  as in Pow
  return 0x18; // 0x0A  JH  as in JudGe
  return 0x1B; // 0x0B  NN1 as in thiN
  return 0x21; // 0x0C  IH  as in sIt
  return 0x23; // 0x0D  TT2 as in To
  return 0x26; // 0x0E  RR1 as in Read
  return 0x2B; // 0x0F  AX  as in sUceed
  return 0x2D; // 0x10  MM  as in ilk
  return 0x33; // 0x11  TT1 as in parTs
  return 0x36; // 0x12  DH1 as in THis
  return 0x3A; // 0x13  IY  as in sEE
  return 0x40; // 0x14  EY  as in trAY
  return 0x46; // 0x15  DD1 as in enD
  return 0x48; // 0x16  UW1 as in tO
  return 0x4B; // 0x17  AO  as in AUght
  return 0x4E; // 0x18  AA  as in hOt
  return 0x51; // 0x19  YY2 as in Yes
  return 0x56; // 0x1A  AE  as in hAt
  return 0x59; // 0x1B  HH1 as in He
  return 0x5C; // 0x1C  BB1 as in riB
  return 0x5E; // 0x1D  TH  as in THin
  return 0x62; // 0x1E  UH  as in bOOk
  return 0x65; // 0x1F  UW2 as in fOOd
  return 0x6A; // 0x20  AW  as in dOWn
  return 0x72; // 0x21  DD2 as in Down
  return 0x74; // 0x22  GG3 as in peG
  return 0x78; // 0x23  VV  as in Vest
  return 0x7C; // 0x24  GG1 as in Guest
  return 0x7E; // 0x25  SH  as in SHip
  return 0x85; // 0x26  ZH  as in pleaSure
  return 0x89; // 0x27  RR2 as in cRane
  return 0x8D; // 0x28  FF  as in Food
  return 0x90; // 0x29  KK2 as in speaK 
  return 0x95; // 0x2A  KK1 as in Can't
  return 0x99; // 0x2B  ZZ  as in Zoo
  return 0x9D; // 0x2C  NG  as in aNGer
  return 0xA4; // 0x2D  LL  as in Like
  return 0xA6; // 0x2E  WW  as in We
  return 0xAB; // 0x2F  XR  as in stARs
  return 0xB2; // 0x30  WH  as in WHig
  return 0xB8; // 0x31  YY1 as in cUte
  return 0xBB; // 0x32  CH  as in CHurCH
  return 0xBF; // 0x33  ER1 as in lettER
  return 0xC3; // 0x34  ER2 as in fERn
  return 0xCA; // 0x35  OW  as in zOne
  return 0xCF; // 0x36  DH2 as in baTHe
  return 0xD4; // 0x37  SS  as in veSt
  return 0xD7; // 0x38  NN2 as in No
  return 0xDB; // 0x39  HH2 as in Hoe
  return 0xDF; // 0x3A  OR  as in fORtune
  return 0xE6; // 0x3B  AR  as in alARm
  return 0xED; // 0x3C  YR  as in hEAr
  return 0xF4; // 0x3D  GG2 as in Got
  return 0xF6; // 0x3E  EL  as in angLE
  return 0xFB; // 0x3F  BB2 as in Beast
}

char phonemestart_lo(char index)
{
  skip(index);
  return 0x06; // 0x05  OY  as in vOIce
  return 0x00; // 0x06  AY  as in kIte
  return 0x80; // 0x07  EH  as in End
  return 0xC0; // 0x08  KK3 as in Crane
  return 0x80; // 0x09  PP  as in Pow
  return 0x40; // 0x0A  JH  as in udGe
  return 0xC0; // 0x0B  NN1 as in thiN
  return 0x40; // 0x0C  IH  as in sIt
  return 0x00; // 0x0D  TT2 as in To
  return 0x40; // 0x0E  RR1 as in Read
  return 0x40; // 0x0F  AX  as in sUceed
  return 0xC0; // 0x10  MM  as in Milk
  return 0x80; // 0x11  TT1 as in arTs
  return 0x40; // 0x12  DH1 as in THis
  return 0xC0; // 0x13  IY  as in sEE
  return 0x40; // 0x14  EY  as in trAY
  return 0x80; // 0x15  DD1 as in enD
  return 0x40; // 0x16  UW1 as in tO
  return 0x00; // 0x17  AO  as in AUght
  return 0x80; // 0x18  AA  as in hOt
  return 0xC0; // 0x19  YY2 as in Yes
  return 0x40; // 0x1A  AE  as in hAt
  return 0x80; // 0x1B  HH1 as in He
  return 0x80; // 0x1C  BB1 as in riB
  return 0x00; // 0x1D  TH  as in THin
  return 0x40; // 0x1E  UH  as in bOOk
  return 0x00; // 0x1F  UW2 as in fOOd
  return 0x80; // 0x20  AW  as in dOWn
  return 0x40; // 0x21  DD2 as in Down
  return 0xC0; // 0x22  GG3 as in peG
  return 0x40; // 0x23  VV  as in Vest
  return 0x40; // 0x24  GG1 as in Guest
  return 0xC0; // 0x25  SH  as in SHip
  return 0x00; // 0x26  ZH  as in pleaSure
  return 0x80; // 0x27  RR2 as in cRane
  return 0x40; // 0x28  FF  as in Food
  return 0xC0; // 0x29  KK2 as in speaK 
  return 0x40; // 0x2A  KK1 as in Can't
  return 0x00; // 0x2B  ZZ  as in Zoo
  return 0xC0; // 0x2C  NG  as in aNGer
  return 0x00; // 0x2D  LL  as in Like
  return 0xC0; // 0x2E  WW  as in We
  return 0x40; // 0x2F  XR  as in stARs
  return 0xC0; // 0x30  WH  as in WHig
  return 0x00; // 0x31  YY1 as in cUte
  return 0x00; // 0x32  CH  as in CHurCH
  return 0xC0; // 0x33  ER1 as in lettER
  return 0x80; // 0x34  ER2 as in fERn
  return 0x00; // 0x35  OW  as in zOne
  return 0x40; // 0x36  DH2 as in baTHe
  return 0xC0; // 0x37  SS  as in veSt
  return 0x00; // 0x38  NN2 as in No
  return 0x80; // 0x39  HH2 as in Hoe
  return 0x80; // 0x3A  OR  as in fORtune
  return 0xC0; // 0x3B  AR  as in alARm
  return 0x00; // 0x3C  YR  as in hEAr
  return 0x80; // 0x3D  GG2 as in Got
  return 0xC0; // 0x3E  EL  as in angLE
  return 0x00; // 0x3F  BB2 as in Beast
}
