# Fritzing sketch pictalker (saved by Fritzing 0.9.3b)
breadboards: 1

parts:
  512 = 24LC512 [chip_label=512 package="DIP (Dual Inline) [THT]"]
  R1 = Resistor [tolerance=±5% resistance=2.2k package=THT]
  C1 = Ceramic Capacitor [capacitance=10nF package="100 mil [THT, multilayer]"]
  R2 = Resistor [tolerance=±5% resistance=4.7k package=THT]
  R3 = Resistor [tolerance=±5% resistance=4.7k package=THT]
  C2 = Ceramic Capacitor [capacitance=10nF package="100 mil [THT, multilayer]"]
  C3 = Ceramic Capacitor [capacitance=100nF package="100 mil [THT, multilayer]"]
  R4 = Resistor [tolerance=±5% resistance=10k package=THT]
  J1 = Piezo Speaker

nets:
  N1: 512.A0, 512.A1, 512.A2, 512.GND, C1.1
  N2: 512.SDA, R1.Pin_1
  N3: 512.WP, 512.VCC, R1.Pin_0
  N4: C1.0, R2.Pin_0, R3.Pin_0
  N5: R3.Pin_1, C2.1, C3.1
  N6: C2.0, R4.Pin_1, J1.pin2
  N7: C3.0, R4.Pin_0, J1.pin1

custom parts:
  24LC512: I2C 8x64k flash memory
